# Fritzing sketch servo (saved by Fritzing 0.9.2b)
circuit board: 8.47cm x 5.64444cm
breadboards: 1

parts:
  U1 = ESP8266 WiFi Module [part_number=ESP8266]
  5V = Power Jack [package=power_jack_pth_lock]
  FTDI = FTDI Basic Programmer
  SERVO = Basic Servo
  Q1 = MOSFET-NCHANNEL [package=to220v]
  PGM = Momentary Switch [package=ksa_sealed_tac_switch]
  RGB = RGB LED (com. cathode, rgb) [package="5 mm [THT]"]
  R9 = Resistor [tolerance=±5% resistance=10k package=THT]
  R1 = Resistor [tolerance=±5% resistance=10k package=THT]
  R2 = Resistor [tolerance=±5% resistance=10k package=THT]
  R4 = Resistor [tolerance=±5% resistance=10k package=THT]
  C1 = Ceramic Capacitor [capacitance="100 nF" package="100 mil [THT, multilayer]"]
  R5 = Resistor [tolerance=±5% resistance=470 package=THT]
  R6 = Resistor [tolerance=±5% resistance=470 package=THT]
  R7 = Resistor [tolerance=±5% resistance=470 package=THT]
  R8 = Resistor [tolerance=±5% resistance=220 package=THT]
  R3 = Resistor [tolerance=±5% resistance=10k package=THT]
  LDO = V_REG_LD1117VXX [package=78xxl]

nets:
  N1: U1.RXD, FTDI.TXO
  N2: U1.VCC, R1.Pin_0, R2.Pin_0, R4.Pin_0, C1.1, R3.Pin_0, LDO.OUT
  N3: U1.GPIO_0, FTDI.DTR, PGM.2, R4.Pin_1
  N4: U1.GPIO_2, R3.Pin_1
  N5: U1.CH_PD, R2.Pin_1
  GND: U1.GND, 5V.GND, FTDI.GND, Q1.S, PGM.4, RGB.common_cathode, R9.Pin_1, C1.0, LDO.GND
  N6: U1.TXD, FTDI.RXI
  N7: U1.GPIO_15, R9.Pin_0
  N8: U1.GPIO_4, R8.Pin_0
  N9: U1.GPIO_5, SERVO.pulse
  N10: U1.GPIO_16, U1.REST, R1.Pin_1
  N11: U1.GPIO_14, R5.Pin_1
  N12: U1.GPIO_12, R6.Pin_1
  N13: U1.GPIO_13, R7.Pin_1
  N14: 5V.PWR, SERVO.vcc, LDO.IN
  N15: SERVO.gnd, Q1.D
  N16: Q1.G, R8.Pin_1
  N17: RGB.red_anode, R5.Pin_0
  N18: RGB.green_anode, R6.Pin_0
  N19: RGB.blue_anode, R7.Pin_0

notes:
  5v rail
  3v3 rail
  WIRE COLORS
  black = ground
  red = power (5v or 3v3)
  blue = programming
  green = stability
  white = devices (servo, led)
  yellow = smd->breadboard
  TODO: perhaps flip FTDI & move PGM north

custom parts:
  ESP8266 WiFi Module: Generic WiFi Module based on the ESP8266 with onboard PCB antenna and UART communications
